// Logisim project simpleRISC_reduced.circ as structural Verilog: 8 circuits, main circuit main
module main (
);

  wire alu_1_alu_is_eq, and_1_out, and_2_out, BSel, call, CLK, FlWEn, halt, I, is_beq, is_ret, is_store,
       IsEq, keyboard_en, LOAD, not_1_out, or_1_out, or_2_out, or_3_out, RegWEn;
  wire [3:0] ALUSel, rs20;
  wire [13:0] IMM_H;
  wire [31:0] ALU_X, ALU_Y, DBUSOUT, dmem_1_dmem_r_data, IMM, multiplexer_7_out, multiplexer_8_out, PC, PC0,
       PC_new, PCnew, PCnew0, ra_reg_q, REG_W_DATA, REG_W_DATA0, rs1_data, rs2_data;
  wire [31:14] INSTRUCTION;

  Clock clock_1 (.out(CLK));
  Register #(.width(32)) u_PC (.D(PCnew), .en(CLK), .clk(CLK), .Q(PC));  // open: clr
  or or_1 (or_1_out, is_beq, call);
  Register #(.width(32)) ra_reg (.D(PC0), .en(call), .clk(CLK), .Q(ra_reg_q));  // open: clr
  Multiplexer #(.width(32)) multiplexer_1 (.in0(rs1_data), .in1(PC), .out(ALU_X), .sel(or_1_out));
  Adder #(.width(32)) adder_1 (.a(32'h4), .b(PC), .out(PC0));  // open: cin, cout
  Multiplexer #(.width(32)) multiplexer_2 (.in0(PC_new), .in1(ra_reg_q), .out(PCnew0), .sel(is_ret));
  Multiplexer #(.width(4)) multiplexer_3 (
    .in0(INSTRUCTION[17:14]), .in1(INSTRUCTION[25:22]), .out(rs20), .sel(is_store));
  or or_2 (or_2_out, and_1_out, call);
  and and_1 (and_1_out, is_beq, IsEq);
  IMEM imem_1 (.IMEM_ADDR(PC), .INSTRUCTION({INSTRUCTION[31:27], I, INSTRUCTION[25:14], IMM_H}));
  Multiplexer #(.width(32)) multiplexer_4 (.in0(PC0), .in1(REG_W_DATA0), .out(PC_new), .sel(or_2_out));
  Multiplexer #(.width(32)) multiplexer_5 (.in0(PCnew0), .in1(PC), .out(PCnew), .sel(halt));
  assign IMM = {{14{INSTRUCTION[17]}}, {INSTRUCTION[17:14], IMM_H}};  // Bit_Extender bit_extender_1
  REGFILE regfile_1 (
    .rs1(INSTRUCTION[21:18]), .rs2(rs20), .rd(INSTRUCTION[25:22]), .REG_W_DATA(REG_W_DATA),
    .WRITE_EN(RegWEn), .CLK(CLK), .rs1_data(rs1_data), .rs2_data(rs2_data));
  Multiplexer #(.width(32)) multiplexer_6 (.in0(rs2_data), .in1(IMM), .out(ALU_Y), .sel(BSel));
  CTRL_ROM ctrl_rom_1 (
    .Opcode(INSTRUCTION[31:27]), .Immediate(I), .IsEq(IsEq), .RegWEn(RegWEn), .BSel(BSel), .FlWEn(FlWEn),
    .ALUSel(ALUSel), .is_store(is_store), .call(call), .LOAD(LOAD), .is_beq(is_beq), .is_ret(is_ret),
    .halt(halt));
  or or_3 (or_3_out, LOAD, is_store);
  not not_1 (not_1_out, CLK);
  and and_2 (and_2_out, or_3_out, not_1_out);
  Multiplexer #(.width(32)) multiplexer_7 (
    .in0({32{1'b0}}), .in1(REG_W_DATA0),
    .out({multiplexer_7_out[31:11], keyboard_en, multiplexer_7_out[9:0]}), .sel(and_2_out));
  ALU alu_1 (.ALU_X(ALU_X), .ALU_Y(ALU_Y), .ALU_OP(ALUSel), .ALU_RESULT(REG_W_DATA0), .ALU_IS_EQ(alu_1_alu_is_eq));
  Register #(.width(1)) u_IsEq (.D(alu_1_alu_is_eq), .en(FlWEn), .clk(CLK), .Q(IsEq));  // open: clr
  MMAPPED_IO mmapped_io_1 (
    .ABUS({multiplexer_7_out[31:11], keyboard_en, multiplexer_7_out[9:0]}), .DBUS_IN(rs2_data), .CLK(CLK),
    .DBUS_OUT(DBUSOUT));
  DMEM dmem_1 (
    .DMEM_ADDR(REG_W_DATA0), .DMEM_W_EN(is_store), .CLK(CLK), .DMEM_W_DATA(rs2_data),
    .DMEM_R_DATA(dmem_1_dmem_r_data));
  Multiplexer #(.width(32)) multiplexer_8 (
    .in0(dmem_1_dmem_r_data), .in1(DBUSOUT), .out(multiplexer_8_out), .sel(keyboard_en));
  Multiplexer #(.width(32)) multiplexer_9 (.in0(REG_W_DATA0), .in1(multiplexer_8_out), .out(REG_W_DATA), .sel(LOAD));

  // Other names for the same wires on the sheet: INSTRUCTION (some bits) = {I, IMM_H}; rs2[3:0] = INSTRUCTION[17:14];
  //   rs1[3:0] = INSTRUCTION[21:18]; rd[3:0] = INSTRUCTION[25:22]; OP[4:0] = INSTRUCTION[31:27]

  // Notes on the sheet:
  //   Fetch
  //   Decode
  //   Execute
  //   Memory Access
  //   Write back
endmodule

module DMEM (
  input  [31:0] DMEM_ADDR,
  input  DMEM_W_EN,
  input  CLK,
  input  [31:0] DMEM_W_DATA,
  output [31:0] DMEM_R_DATA
);

  RAM #(.addrWidth(10), .dataWidth(32), .enables("line")) ram_1 (
    .addr(DMEM_ADDR[9:0]), .we(DMEM_W_EN), .clk(CLK), .din(DMEM_W_DATA), .dout(DMEM_R_DATA));

  // Other names for the same wires on the sheet: DMEM_READ_DATA[31:0] = DMEM_R_DATA;
  //   DMEM_WRITE_DATA[31:0] = DMEM_W_DATA; DMEM_WRITE_EN = DMEM_W_EN
endmodule

module IMEM (
  input  [31:0] IMEM_ADDR,
  output [31:0] INSTRUCTION
);

  // ROM #(.addrWidth(10), .line("quad")) rom_1: pin names not known; wires that end beside it: IMEM_ADDR[9:0], INSTRUCTION[7:0], INSTRUCTION[15:8], INSTRUCTION[23:16], INSTRUCTION[31:24]
endmodule

module REGFILE (
  input  [3:0] rs1,
  input  [3:0] rs2,
  input  [3:0] rd,
  input  [31:0] REG_W_DATA,
  input  WRITE_EN,
  input  CLK,
  output [31:0] rs1_data,
  output [31:0] rs2_data
);

  wire WE_1, WE_2, WE_3, WE_4, WE_5, WE_6, WE_7, WE_8, WE_9, WE_10, WE_11, WE_12, WE_13, WE_14, WE_15, WE_16,
       WE_17, WE_18, WE_19, WE_20, WE_21, WE_22, WE_23, WE_24, WE_25, WE_26, WE_27, WE_28, WE_29, WE_30,
       WE_31;
  wire [31:0] in_r1, in_r2, in_r3, in_r4, in_r5, in_r6, in_r7, in_r8, in_r9, in_r10, in_r11, in_r12, in_r13,
       in_r14, in_r15, in_r16, in_r17, in_r18, in_r19, in_r20, in_r21, in_r22, in_r23, in_r24, in_r25,
       in_r26, in_r27, in_r28, in_r29, in_r30, in_r31, out_r1, out_r2, out_r3, out_r4, out_r5, out_r6,
       out_r7, out_r8, out_r9, out_r10, out_r11, out_r12, out_r13, out_r14, out_r15, out_r16, out_r17,
       out_r18, out_r19, out_r20, out_r21, out_r22, out_r23, out_r24, out_r25, out_r26, out_r27, out_r28,
       out_r29, out_r30, out_r31;

  // LedBar #(.inputtype("row"), .matrixcols(5)) ledbar_1: pin names not known; wires that end beside it: {1'b0, rd}
  // LedBar #(.inputtype("row"), .matrixcols(5)) ledbar_2: pin names not known; wires that end beside it: {1'b0, rs1}
  // LedBar #(.inputtype("row"), .matrixcols(5)) ledbar_3: pin names not known; wires that end beside it: {1'b0, rs2}
  Register #(.width(32)) r1 (.D(in_r1), .en(WE_1), .clk(CLK), .Q(out_r1));  // open: clr
  Register #(.width(32)) register_1 (.D(in_r9), .en(WE_9), .clk(CLK), .Q(out_r9));  // open: clr
  Register #(.width(32)) register_2 (.D(in_r17), .en(WE_17), .clk(CLK), .Q(out_r17));  // open: clr
  Register #(.width(32)) register_3 (.D(in_r25), .en(WE_25), .clk(CLK), .Q(out_r25));  // open: clr
  Multiplexer #(.select(5), .width(32)) multiplexer_1 (
    .in0({32{1'b0}}), .in1(out_r1), .in2(out_r2), .in3(out_r3), .in4(out_r4), .in5(out_r5), .in6(out_r6),
    .in7(out_r7), .in8(out_r8), .in9(out_r9), .in10(out_r10), .in11(out_r11), .in12(out_r12), .in13(out_r13),
    .in14(out_r14), .in15(out_r15), .in16(out_r16), .in17(out_r17), .in18(out_r18), .in19(out_r19),
    .in20(out_r20), .in21(out_r21), .in22(out_r22), .in23(out_r23), .in24(out_r24), .in25(out_r25),
    .in26(out_r26), .in27(out_r27), .in28(out_r28), .in29(out_r29), .in30(out_r30), .in31(out_r31),
    .out(rs1_data), .sel({1'b0, rs1}));
  Register #(.width(32)) r2 (.D(in_r2), .en(WE_2), .clk(CLK), .Q(out_r2));  // open: clr
  Register #(.width(32)) register_4 (.D(in_r10), .en(WE_10), .clk(CLK), .Q(out_r10));  // open: clr
  Register #(.width(32)) register_5 (.D(in_r18), .en(WE_18), .clk(CLK), .Q(out_r18));  // open: clr
  Register #(.width(32)) register_6 (.D(in_r26), .en(WE_26), .clk(CLK), .Q(out_r26));  // open: clr
  Register #(.width(32)) r3 (.D(in_r3), .en(WE_3), .clk(CLK), .Q(out_r3));  // open: clr
  Register #(.width(32)) register_7 (.D(in_r11), .en(WE_11), .clk(CLK), .Q(out_r11));  // open: clr
  Register #(.width(32)) register_8 (.D(in_r19), .en(WE_19), .clk(CLK), .Q(out_r19));  // open: clr
  Register #(.width(32)) register_9 (.D(in_r27), .en(WE_27), .clk(CLK), .Q(out_r27));  // open: clr
  Multiplexer #(.select(5), .width(32)) multiplexer_2 (
    .in0({32{1'b0}}), .in1(out_r1), .in2(out_r2), .in3(out_r3), .in4(out_r4), .in5(out_r5), .in6(out_r6),
    .in7(out_r7), .in8(out_r8), .in9(out_r9), .in10(out_r10), .in11(out_r11), .in12(out_r12), .in13(out_r13),
    .in14(out_r14), .in15(out_r15), .in16(out_r16), .in17(out_r17), .in18(out_r18), .in19(out_r19),
    .in20(out_r20), .in21(out_r21), .in22(out_r22), .in23(out_r23), .in24(out_r24), .in25(out_r25),
    .in26(out_r26), .in27(out_r27), .in28(out_r28), .in29(out_r29), .in30(out_r30), .in31(out_r31),
    .out(rs2_data), .sel({1'b0, rs2}));
  Register #(.width(32)) r4 (.D(in_r4), .en(WE_4), .clk(CLK), .Q(out_r4));  // open: clr
  Register #(.width(32)) register_10 (.D(in_r12), .en(WE_12), .clk(CLK), .Q(out_r12));  // open: clr
  Register #(.width(32)) register_11 (.D(in_r20), .en(WE_20), .clk(CLK), .Q(out_r20));  // open: clr
  Register #(.width(32)) register_12 (.D(in_r28), .en(WE_28), .clk(CLK), .Q(out_r28));  // open: clr
  Demultiplexer #(.enable("true"), .select(5), .width(32)) demultiplexer_1 (
    .out1(in_r1), .out2(in_r2), .out3(in_r3), .out4(in_r4), .out5(in_r5), .out6(in_r6), .out7(in_r7),
    .out8(in_r8), .out9(in_r9), .out10(in_r10), .out11(in_r11), .out12(in_r12), .out13(in_r13),
    .out14(in_r14), .out15(in_r15), .out16(in_r16), .out17(in_r17), .out18(in_r18), .out19(in_r19),
    .out20(in_r20), .out21(in_r21), .out22(in_r22), .out23(in_r23), .out24(in_r24), .out25(in_r25),
    .out26(in_r26), .out27(in_r27), .out28(in_r28), .out29(in_r29), .out30(in_r30), .out31(in_r31),
    .in(REG_W_DATA), .sel({1'b0, rd}), .en(WRITE_EN));  // open: out0
  Register #(.width(32)) r5 (.D(in_r5), .en(WE_5), .clk(CLK), .Q(out_r5));  // open: clr
  Register #(.width(32)) register_13 (.D(in_r13), .en(WE_13), .clk(CLK), .Q(out_r13));  // open: clr
  Register #(.width(32)) register_14 (.D(in_r21), .en(WE_21), .clk(CLK), .Q(out_r21));  // open: clr
  Register #(.width(32)) register_15 (.D(in_r29), .en(WE_29), .clk(CLK), .Q(out_r29));  // open: clr
  Register #(.width(32)) register_16 (.D(in_r6), .en(WE_6), .clk(CLK), .Q(out_r6));  // open: clr
  Register #(.width(32)) register_17 (.D(in_r14), .en(WE_14), .clk(CLK), .Q(out_r14));  // open: clr
  Register #(.width(32)) register_18 (.D(in_r22), .en(WE_22), .clk(CLK), .Q(out_r22));  // open: clr
  Register #(.width(32)) register_19 (.D(in_r30), .en(WE_30), .clk(CLK), .Q(out_r30));  // open: clr
  Decoder #(.select(5)) decoder_1 (
    .out1(WE_1), .out2(WE_2), .out3(WE_3), .out4(WE_4), .out5(WE_5), .out6(WE_6), .out7(WE_7), .out8(WE_8),
    .out9(WE_9), .out10(WE_10), .out11(WE_11), .out12(WE_12), .out13(WE_13), .out14(WE_14), .out15(WE_15),
    .out16(WE_16), .out17(WE_17), .out18(WE_18), .out19(WE_19), .out20(WE_20), .out21(WE_21), .out22(WE_22),
    .out23(WE_23), .out24(WE_24), .out25(WE_25), .out26(WE_26), .out27(WE_27), .out28(WE_28), .out29(WE_29),
    .out30(WE_30), .out31(WE_31), .sel({1'b0, rd}), .en(WRITE_EN));  // open: out0
  Register #(.width(32)) register_20 (.D(in_r7), .en(WE_7), .clk(CLK), .Q(out_r7));  // open: clr
  Register #(.width(32)) register_21 (.D(in_r15), .en(WE_15), .clk(CLK), .Q(out_r15));  // open: clr
  Register #(.width(32)) register_22 (.D(in_r23), .en(WE_23), .clk(CLK), .Q(out_r23));  // open: clr
  Register #(.width(32)) register_23 (.D(in_r31), .en(WE_31), .clk(CLK), .Q(out_r31));  // open: clr
  Register #(.width(32)) register_24 (.D(in_r8), .en(WE_8), .clk(CLK), .Q(out_r8));  // open: clr
  Register #(.width(32)) register_25 (.D(in_r16), .en(WE_16), .clk(CLK), .Q(out_r16));  // open: clr
  Register #(.width(32)) register_26 (.D(in_r24), .en(WE_24), .clk(CLK), .Q(out_r24));  // open: clr

  // Other names for the same wires on the sheet: reg1[3:0] = rs1; reg1_data[31:0] = rs1_data; reg2[3:0] = rs2;
  //   reg2_data[31:0] = rs2_data; reg_write[3:0] = rd; reg_write_data[31:0] = REG_W_DATA; WE = WRITE_EN

  // Notes on the sheet:
  //   Outputs
  //   I/O
  //   Inputs
  //   Register Reading
  //   Register Writing
endmodule

module ALU (
  input  [31:0] ALU_X,
  input  [31:0] ALU_Y,
  input  [3:0] ALU_OP,
  output [31:0] ALU_RESULT,
  output ALU_IS_EQ
);

  wire comparator_1_lt;
  wire [31:0] o_add, o_and, o_div, o_mul, o_mulh, o_or, o_rem, o_sll, o_slt, o_srl, o_sub, o_xor;

  Multiplexer #(.select(4), .width(32)) multiplexer_1 (
    .in0(o_add), .in1(o_sub), .in2(o_and), .in3(o_or), .in4(o_xor), .in5(o_sll), .in6(o_srl), .in7(o_mul),
    .in8(o_mulh), .in9(o_div), .in10(o_rem), .in11(o_slt), .out(ALU_RESULT), .sel(ALU_OP));  // open: in12, in13, in14, in15
  Adder #(.width(32)) adder_1 (.a(ALU_X), .b(ALU_Y), .out(o_add));  // open: cin, cout
  Subtractor #(.width(32)) subtractor_1 (.a(ALU_X), .b(ALU_Y), .out(o_sub));  // open: bin, bout
  assign o_and = ALU_X & ALU_Y;  // AND_Gate and_1, 32 bits wide
  assign o_or = ALU_X | ALU_Y;  // OR_Gate or_1, 32 bits wide
  assign o_xor = ALU_X ^ ALU_Y;  // XOR_Gate xor_1, 32 bits wide
  Shifter #(.width(32)) shifter_1 (.in(ALU_X), .\dist (ALU_Y[4:0]), .out(o_sll));
  Comparator #(.width(32)) comparator_1 (.a(ALU_X), .b(ALU_Y), .lt(comparator_1_lt));  // open: gt, eq
  Shifter #(.shift("lr"), .width(32)) shifter_2 (.in(ALU_X), .\dist (ALU_Y[4:0]), .out(o_srl));
  Multiplier #(.width(32)) multiplier_1 (.a(ALU_X), .b(ALU_Y), .out(o_mul));  // open: cin, cout
  Multiplier #(.width(32)) multiplier_2 (.a(ALU_X), .b(ALU_Y), .cout(o_mulh));  // open: out, cin
  Divider #(.width(32)) divider_1 (.a(ALU_X), .b(ALU_Y), .out(o_div));  // open: upper, rem
  Divider #(.width(32)) divider_2 (.a(ALU_X), .b(ALU_Y), .rem(o_rem));  // open: out, upper
  Comparator #(.width(32)) comparator_2 (.a(ALU_X), .b(ALU_Y), .eq(ALU_IS_EQ));  // open: gt, lt
  Bit_Extender #(.in_width(1), .out_width(32)) bit_extender_1 (.out(o_slt));  // open: in

  // Other names for the same wires on the sheet: isEqual = ALU_IS_EQ; OP[3:0] = ALU_OP; result[31:0] = ALU_RESULT;
  //   X[31:0] = ALU_X; Y[31:0] = ALU_Y

  // Notes on the sheet:
  //   Outputs
  //   I/O
  //   Operation Selection
  //   Inputs
  //   Operations
endmodule

module CTRL_COMBI (
  input  [4:0] Opcode,
  input  Immediate,
  input  IsEq,
  output RegWEn,
  output BSel,
  output FlWEn,
  output [3:0] ALUSel,
  output is_store,
  output call,
  output LOAD,
  output is_beq,
  output is_ret,
  output halt
);

  wire ADD, SUB;

  Multiplexer #(.select(5), .width(4)) multiplexer_1 (
    .in0(4'b0000), .in1(4'b0001), .in14(4'b0000), .in15(4'b0000), .in16(4'b0000), .in19(4'b0000),
    .out(ALUSel), .sel(Opcode));  // open: in2, in3, in4, in5, in6, in7, in8, in9, in10, in11, in12, in13, in17, in18, in20, in21, in22, in23, in24, in25, in26, in27, in28, in29, in30, in31
  Comparator #(.width(5)) comparator_1 (.a(Opcode), .b({5{1'b1}}), .eq(halt));  // open: gt, lt
  Comparator #(.width(5)) comparator_2 (.a(Opcode), .b(5'b01111), .eq(is_store));  // open: gt, lt
  Comparator #(.width(5)) comparator_3 (.a(Opcode), .b(5'b10011), .eq(call));  // open: gt, lt
  Comparator #(.width(5)) comparator_4 (.a(Opcode), .b(5'b10000), .eq(is_beq));  // open: gt, lt
  Comparator #(.width(5)) comparator_5 (.a(Opcode), .b(5'b10100), .eq(is_ret));  // open: gt, lt
  Comparator #(.width(5)) comparator_6 (.a(Opcode), .b({5{1'b0}}), .eq(ADD));  // open: gt, lt
  Comparator #(.width(5)) comparator_7 (.a(Opcode), .b(5'b00001), .eq(SUB));  // open: gt, lt
  Comparator #(.width(5)) comparator_8 (.a(Opcode), .b(5'b00101), .eq(FlWEn));  // open: gt, lt
  Comparator #(.width(5)) comparator_9 (.a(Opcode), .b(5'b01110), .eq(LOAD));  // open: gt, lt
  or or_1 (RegWEn, ADD, LOAD, SUB);

  assign BSel = Immediate;

  // Other names for the same wires on the sheet: CMP = FlWEn; I = Immediate; OP[4:0] = Opcode

  // Notes on the sheet:
  //   ALU Operation select (ALUSel)
  //   This data goes to datapath
  //   Connections to control unit
  //   This data comes to control unit
  //   Instruction decoding
  //   ALU_Y operand select (BSel)
  //   Register file writeback enable
  //   Flag writeback enable
endmodule

module CTRL_ROM (
  input  [4:0] Opcode,
  input  Immediate,
  input  IsEq,
  output RegWEn,
  output BSel,
  output FlWEn,
  output [3:0] ALUSel,
  output is_store,
  output call,
  output LOAD,
  output is_beq,
  output is_ret,
  output halt
);

  wire [2:0] rom_1_data;

  ROM #(.addrWidth(7), .dataWidth(16)) rom_1 (
    .addr({Opcode, Immediate, IsEq}),
    .data({RegWEn, BSel, FlWEn, ALUSel, is_store, call, LOAD, is_beq, is_ret, halt, rom_1_data}));

  // Other names for the same wires on the sheet: I = Immediate; OP[4:0] = Opcode

  // Notes on the sheet:
  //   This data goes to datapath
  //   Connections to control unit
  //   This data comes to control unit
  //   contents of rom_1 (hex, n*v repeats v):
  //   0 0 c000 17*0 2000 37*0 c040 0 0 0 4100 4*0 4020 11*0 4080
endmodule

module MMAPPED_IO (
  input  [31:0] ABUS,
  input  [31:0] DBUS_IN,
  input  CLK,
  output [31:0] DBUS_OUT
);

  wire and_1_out, and_3_out, and_4_out, not_1_out, READ_EN;
  wire [6:0] keyboard_1_data;
  wire [31:0] DATA, register_1_q, register_3_q, STATUS;

  Register #(.width(32)) register_1 (.D(DBUS_IN), .en(and_1_out), .clk(CLK), .Q(register_1_q));  // open: clr
  and and_1 (and_1_out, ABUS[2], ABUS[10]);
  and and_2 (READ_EN, ABUS[3], ABUS[10]);
  Keyboard keyboard_1 (.clk(READ_EN), .re(1'b1), .clr(register_1_q[0]), .avail(STATUS[0]), .data(keyboard_1_data));
  not not_1 (not_1_out, and_1_out);
  Multiplexer #(.disabled("Z"), .enable("true"), .width(32)) multiplexer_1 (
    .in0(STATUS), .in1(DATA), .out(DBUS_OUT), .sel(READ_EN), .en(not_1_out));
  Register #(.width(7)) register_2 (.D(keyboard_1_data), .en(READ_EN), .clk(READ_EN), .Q(DATA[6:0]));  // open: clr
  and and_3 (and_3_out, ABUS[2], ABUS[11]);
  and and_4 (and_4_out, ABUS[3], ABUS[11]);
  Register #(.width(32)) register_3 (.D(DBUS_IN), .en(and_3_out), .clk(CLK), .Q(register_3_q));  // open: clr
  TTY tty_1 (.data(DBUS_IN[6:0]), .clk(CLK), .we(and_4_out), .clr(register_3_q[0]));

  // Other names for the same wires on the sheet: CTRL_ADD = ABUS[2]; DATA_ADD = ABUS[3]; KBD_EN = ABUS[10];
  //   TTY_EN = ABUS[11]

  // Notes on the sheet:
  //   Poke here v to enter keyboard data and see the results here v
endmodule
